// Logisim project Nand Gates.circ as structural Verilog: 32 circuits, main circuit Not
module Not (
  input  in_1,
  output out_2
);

  nand nand_1 (out_2, in_1, in_1);

  // Notes on the sheet:
  //   Not Gate
endmodule

module And (
  input  in_1,
  input  in_2,
  output out_3
);

  wire nand_1_out;

  nand nand_1 (nand_1_out, in_1, in_2);
  nand nand_2 (out_3, nand_1_out, nand_1_out);

  // Notes on the sheet:
  //   And gate
endmodule

module Or (
  input  in_1,
  input  in_2,
  output out_3
);

  wire nand_1_out, nand_2_out;

  nand nand_1 (nand_1_out, in_1, in_1);
  nand nand_2 (nand_2_out, in_2, in_2);
  nand nand_3 (out_3, nand_1_out, nand_2_out);

  // Notes on the sheet:
  //   Or Gate
endmodule

module Mux (
  input  A,
  input  Sel,
  input  B,
  output out_4
);

  wire and_1_out, and_2_out, not_1_out;

  and and_1 (and_1_out, A, not_1_out);
  not not_1 (not_1_out, Sel);
  or or_1 (out_4, and_1_out, and_2_out);
  and and_2 (and_2_out, Sel, B);
endmodule

module DMux (
  input  in_1,
  input  in_2,
  output Out,
  output out_4
);

  wire not_1_out;

  and and_1 (Out, in_1, not_1_out);
  not not_1 (not_1_out, in_2);
  and and_2 (out_4, in_2, in_1);
endmodule

module Xor (
  input  in_1,
  input  in_2,
  output out_3
);

  wire and_1_out, and_2_out, not_1_out, not_2_out;

  not not_1 (not_1_out, in_1);
  not not_2 (not_2_out, in_2);
  and and_1 (and_1_out, in_1, not_2_out);
  and and_2 (and_2_out, not_1_out, in_2);
  or or_1 (out_3, and_1_out, and_2_out);
endmodule

module And16 (
  input  [15:0] A,
  input  [15:0] B,
  output [15:0] Out
);

  and _15 (Out[15], A[15], B[15]);
  and _12 (Out[12], A[12], B[12]);
  and _14 (Out[14], A[14], B[14]);
  and _13 (Out[13], A[13], B[13]);
  and _9 (Out[9], A[9], B[9]);
  and _11 (Out[11], A[11], B[11]);
  and _10 (Out[10], A[10], B[10]);
  and _7 (Out[7], A[7], B[7]);
  and _8 (Out[8], A[8], B[8]);
  and _4 (Out[4], A[4], B[4]);
  and _6 (Out[6], A[6], B[6]);
  and _5 (Out[5], A[5], B[5]);
  and _1 (Out[1], A[1], B[1]);
  and _2 (Out[2], A[2], B[2]);
  and _3 (Out[3], A[3], B[3]);
  and _0 (Out[0], A[0], B[0]);

  // Notes on the sheet:
  //   And16
endmodule

module Not16 (
  input  [15:0] in_1,
  output [15:0] out_2
);

  not not_1 (out_2[0], in_1[0]);
  not not_2 (out_2[1], in_1[1]);
  not not_3 (out_2[2], in_1[2]);
  not not_4 (out_2[3], in_1[3]);
  not not_5 (out_2[4], in_1[4]);
  not not_6 (out_2[5], in_1[5]);
  not not_7 (out_2[6], in_1[6]);
  not not_8 (out_2[7], in_1[7]);
  not not_9 (out_2[8], in_1[8]);
  not not_10 (out_2[9], in_1[9]);
  not not_11 (out_2[10], in_1[10]);
  not not_12 (out_2[11], in_1[11]);
  not not_13 (out_2[12], in_1[12]);
  not not_14 (out_2[13], in_1[13]);
  not not_15 (out_2[14], in_1[14]);
  not not_16 (out_2[15], in_1[15]);

  // Notes on the sheet:
  //   In
  //   Not16
  //   Out
endmodule

module Or16 (
  input  [15:0] A,
  input  [15:0] B,
  output [15:0] Out
);

  or _15 (Out[15], A[15], B[15]);
  or _13 (Out[13], A[13], B[13]);
  or _14 (Out[14], A[14], B[14]);
  or _12 (Out[12], A[12], B[12]);
  or _10 (Out[10], A[10], B[10]);
  or _9 (Out[9], A[9], B[9]);
  or _11 (Out[11], A[11], B[11]);
  or _7 (Out[7], A[7], B[7]);
  or _8 (Out[8], A[8], B[8]);
  or _4 (Out[4], A[4], B[4]);
  or _5 (Out[5], A[5], B[5]);
  or _6 (Out[6], A[6], B[6]);
  or _1 (Out[1], A[1], B[1]);
  or _3 (Out[3], A[3], B[3]);
  or _2 (Out[2], A[2], B[2]);
  or _0 (Out[0], A[0], B[0]);

  // Notes on the sheet:
  //   Or16
endmodule

module Mux16 (
  input  [15:0] in_1,
  input  Sel,
  input  [15:0] B,
  output [15:0] Out
);

  wire and_1_out, and_2_out, and_3_out, and_4_out, and_5_out, and_6_out, and_7_out, and_8_out, and_9_out,
       and_10_out, and_11_out, and_12_out, and_13_out, and_14_out, and_15_out, and_16_out, and_17_out,
       and_18_out, and_19_out, and_20_out, and_21_out, and_22_out, and_23_out, and_24_out, and_25_out,
       and_26_out, and_27_out, and_28_out, and_29_out, and_30_out, and_31_out, and_32_out, not_1_out,
       not_2_out, not_3_out, not_4_out, not_5_out, not_6_out, not_7_out, not_8_out, not_9_out, not_10_out,
       not_11_out, not_12_out, not_13_out, not_14_out, not_15_out, not_16_out;

  and and_1 (and_1_out, in_1[0], not_1_out);
  not not_1 (not_1_out, Sel);
  and and_2 (and_2_out, Sel, B[0]);
  and and_3 (and_3_out, in_1[1], not_2_out);
  not not_2 (not_2_out, Sel);
  and and_4 (and_4_out, Sel, B[1]);
  and and_5 (and_5_out, in_1[2], not_3_out);
  not not_3 (not_3_out, Sel);
  and and_6 (and_6_out, Sel, B[2]);
  and and_7 (and_7_out, in_1[3], not_4_out);
  not not_4 (not_4_out, Sel);
  and and_8 (and_8_out, Sel, B[3]);
  not not_5 (not_5_out, Sel);
  not not_6 (not_6_out, Sel);
  not not_7 (not_7_out, Sel);
  not not_8 (not_8_out, Sel);
  or or_1 (Out[0], and_1_out, and_2_out);
  or or_2 (Out[1], and_3_out, and_4_out);
  or or_3 (Out[2], and_5_out, and_6_out);
  or or_4 (Out[3], and_7_out, and_8_out);
  and and_9 (and_9_out, in_1[4], not_5_out);
  or or_5 (Out[4], and_9_out, and_10_out);
  and and_10 (and_10_out, Sel, B[4]);
  and and_11 (and_11_out, in_1[5], not_6_out);
  or or_6 (Out[5], and_11_out, and_12_out);
  and and_12 (and_12_out, Sel, B[5]);
  and and_13 (and_13_out, in_1[6], not_7_out);
  or or_7 (Out[6], and_13_out, and_14_out);
  and and_14 (and_14_out, Sel, B[6]);
  and and_15 (and_15_out, in_1[8], not_8_out);
  or or_8 (Out[7], and_15_out, and_16_out);
  and and_16 (and_16_out, Sel, B[7]);
  and and_17 (and_17_out, in_1[8], not_9_out);
  not not_9 (not_9_out, Sel);
  and and_18 (and_18_out, Sel, B[8]);
  and and_19 (and_19_out, in_1[9], not_10_out);
  not not_10 (not_10_out, Sel);
  and and_20 (and_20_out, Sel, B[9]);
  and and_21 (and_21_out, in_1[10], not_11_out);
  not not_11 (not_11_out, Sel);
  and and_22 (and_22_out, Sel, B[10]);
  and and_23 (and_23_out, in_1[11], not_12_out);
  not not_12 (not_12_out, Sel);
  and and_24 (and_24_out, Sel, B[11]);
  not not_13 (not_13_out, Sel);
  not not_14 (not_14_out, Sel);
  not not_15 (not_15_out, Sel);
  not not_16 (not_16_out, Sel);
  or or_9 (Out[8], and_17_out, and_18_out);
  or or_10 (Out[9], and_19_out, and_20_out);
  or or_11 (Out[10], and_21_out, and_22_out);
  or or_12 (Out[11], and_23_out, and_24_out);
  and and_25 (and_25_out, in_1[12], not_13_out);
  or or_13 (Out[12], and_25_out, and_26_out);
  and and_26 (and_26_out, Sel, B[12]);
  and and_27 (and_27_out, in_1[13], not_14_out);
  or or_14 (Out[13], and_27_out, and_28_out);
  and and_28 (and_28_out, Sel, B[13]);
  and and_29 (and_29_out, in_1[14], not_15_out);
  or or_15 (Out[14], and_29_out, and_30_out);
  and and_30 (and_30_out, Sel, B[14]);
  and and_31 (and_31_out, in_1[15], not_16_out);
  or or_16 (Out[15], and_31_out, and_32_out);
  and and_32 (and_32_out, Sel, B[15]);

  assign in_1[7] = in_1[8];

  // Notes on the sheet:
  //   A
endmodule

module Or8Way (
  input  [7:0] in_1,
  output Out
);

  wire or_1_out, or_2_out, or_3_out, or_4_out, or_5_out, or_6_out;

  or or_1 (or_1_out, in_1[0], in_1[1]);
  or or_2 (or_2_out, or_1_out, in_1[2]);
  or or_3 (or_3_out, or_2_out, in_1[3]);
  or or_4 (or_4_out, or_3_out, in_1[4]);
  or or_5 (or_5_out, or_4_out, in_1[5]);
  or or_6 (or_6_out, or_5_out, in_1[6]);
  or or_7 (Out, or_6_out, in_1[7]);

  // Notes on the sheet:
  //   IN
  //   Or8Way
endmodule

module Mux4Way16 (
  input  [15:0] in_1,
  input  [15:0] in_2,
  input  [1:0] Sel,
  input  [15:0] in_4,
  input  [15:0] in_5
);

  wire [15:0] Mux16_2_out, Mux16_3_out, Mux16_out;

  Mux16 Mux16 (.in_1(in_1), .Sel(Sel[0]), .B(in_2), .Out(Mux16_out));
  Mux16 Mux16_2 (.in_1(in_4), .Sel(Sel[0]), .B(in_5), .Out(Mux16_2_out));
  Mux16 Mux16_3 (.in_1(Mux16_out), .Sel(Sel[1]), .B(Mux16_2_out), .Out(Mux16_3_out));
  // Probe on Mux16_3_out

  // Notes on the sheet:
  //   A
  //   B
  //   C
  //   D
  //   Mux4Way16
  //   Out
endmodule

module Mux8Way16 (
  input  [15:0] a,
  input  [15:0] b,
  input  [15:0] c,
  input  [15:0] d,
  input  [2:0] sel,
  input  [15:0] e,
  input  [15:0] f,
  input  [15:0] g,
  input  [15:0] h
);

  wire [15:0] Mux16_2_out, Mux16_3_out, Mux16_4_out, Mux16_5_out, Mux16_6_out, Mux16_7_out, Mux16_out;

  Mux16 Mux16 (.in_1(a), .Sel(sel[0]), .B(b), .Out(Mux16_out));
  Mux16 Mux16_2 (.in_1(c), .Sel(sel[0]), .B(d), .Out(Mux16_2_out));
  Mux16 Mux16_3 (.in_1(e), .Sel(sel[0]), .B(f), .Out(Mux16_3_out));
  Mux16 Mux16_4 (.in_1(Mux16_3_out), .Sel(sel[1]), .B(Mux16_5_out), .Out(Mux16_4_out));
  Mux16 Mux16_5 (.in_1(g), .Sel(sel[0]), .B(h), .Out(Mux16_5_out));
  Mux16 Mux16_6 (.in_1(Mux16_out), .Sel(sel[1]), .B(Mux16_2_out), .Out(Mux16_6_out));
  Mux16 Mux16_7 (.in_1(Mux16_6_out), .Sel(sel[2]), .B(Mux16_4_out), .Out(Mux16_7_out));
  // Probe on Mux16_7_out

  // Notes on the sheet:
  //   Mux8Way16
endmodule

module DMux4Way (
  input  In,
  input  [1:0] Sel
);

  wire DMux_2_out, DMux_2_out_4, DMux_3_out, DMux_3_out_4, DMux_out, DMux_out_4;

  DMux DMux (.in_1(In), .in_2(Sel[1]), .Out(DMux_out), .out_4(DMux_out_4));
  // Probe on DMux_2_out
  DMux DMux_2 (.in_1(DMux_out), .in_2(Sel[0]), .Out(DMux_2_out), .out_4(DMux_2_out_4));
  // Probe on DMux_2_out_4
  // Probe on DMux_3_out
  DMux DMux_3 (.in_1(DMux_out_4), .in_2(Sel[0]), .Out(DMux_3_out), .out_4(DMux_3_out_4));
  // Probe on DMux_3_out_4

  // Notes on the sheet:
  //   Mux4Way
endmodule

module DMux8Way (
  input  In,
  input  [2:0] Sel
);

  wire demultiplexer_1_out0, demultiplexer_1_out1, demultiplexer_2_out0, demultiplexer_2_out1,
       demultiplexer_3_out0, demultiplexer_3_out1, demultiplexer_4_out0, demultiplexer_4_out1,
       demultiplexer_5_out1, demultiplexer_6_out0, demultiplexer_6_out1, demultiplexer_7_out0,
       demultiplexer_7_out1, undriven;

  Demultiplexer #(.enable("false")) demultiplexer_1 (
    .out0(demultiplexer_1_out0), .out1(demultiplexer_1_out1), .in(In), .sel(Sel[0]));
  Demultiplexer #(.enable("false")) demultiplexer_2 (
    .out0(demultiplexer_2_out0), .out1(demultiplexer_2_out1), .in(demultiplexer_1_out0), .sel(Sel[1]));
  Demultiplexer #(.enable("false")) demultiplexer_3 (
    .out0(demultiplexer_3_out0), .out1(demultiplexer_3_out1), .in(demultiplexer_1_out1), .sel(Sel[1]));
  // Probe on demultiplexer_4_out0
  Demultiplexer #(.enable("false")) demultiplexer_4 (
    .out0(demultiplexer_4_out0), .out1(demultiplexer_4_out1), .in(demultiplexer_2_out0), .sel(Sel[2]));
  // Probe on demultiplexer_4_out1
  // Probe on undriven
  Demultiplexer #(.enable("false")) demultiplexer_5 (
    .out1(demultiplexer_5_out1), .in(demultiplexer_2_out1), .sel(Sel[2]));  // open: out0
  // Probe on demultiplexer_5_out1
  Demultiplexer #(.enable("false")) demultiplexer_6 (
    .out0(demultiplexer_6_out0), .out1(demultiplexer_6_out1), .in(demultiplexer_3_out0), .sel(Sel[2]));
  // Probe on demultiplexer_6_out0
  // Probe on demultiplexer_6_out1
  Demultiplexer #(.enable("false")) demultiplexer_7 (
    .out0(demultiplexer_7_out0), .out1(demultiplexer_7_out1), .in(demultiplexer_3_out1), .sel(Sel[2]));
  // Probe on demultiplexer_7_out0
  // Probe on demultiplexer_7_out1

  // Notes on the sheet:
  //   DMux8Way
endmodule

module DMux8Way16 (
  input  In,
  input  [2:0] Sel
);

  wire demultiplexer_1_out0, demultiplexer_1_out1, demultiplexer_2_out0, demultiplexer_2_out1,
       demultiplexer_3_out0, demultiplexer_3_out1, demultiplexer_4_out0, demultiplexer_4_out1,
       demultiplexer_5_out1, demultiplexer_6_out0, demultiplexer_6_out1, demultiplexer_7_out0,
       demultiplexer_7_out1, undriven;

  Demultiplexer #(.enable("false")) demultiplexer_1 (
    .out0(demultiplexer_1_out0), .out1(demultiplexer_1_out1), .in(In), .sel(Sel[0]));
  Demultiplexer #(.enable("false")) demultiplexer_2 (
    .out0(demultiplexer_2_out0), .out1(demultiplexer_2_out1), .in(demultiplexer_1_out0), .sel(Sel[1]));
  Demultiplexer #(.enable("false")) demultiplexer_3 (
    .out0(demultiplexer_3_out0), .out1(demultiplexer_3_out1), .in(demultiplexer_1_out1), .sel(Sel[1]));
  // Probe on demultiplexer_4_out0
  Demultiplexer #(.enable("false")) demultiplexer_4 (
    .out0(demultiplexer_4_out0), .out1(demultiplexer_4_out1), .in(demultiplexer_2_out0), .sel(Sel[2]));
  // Probe on demultiplexer_4_out1
  // Probe on undriven
  Demultiplexer #(.enable("false")) demultiplexer_5 (
    .out1(demultiplexer_5_out1), .in(demultiplexer_2_out1), .sel(Sel[2]));  // open: out0
  // Probe on demultiplexer_5_out1
  // Probe on demultiplexer_6_out0
  Demultiplexer #(.enable("false")) demultiplexer_6 (
    .out0(demultiplexer_6_out0), .out1(demultiplexer_6_out1), .in(demultiplexer_3_out0), .sel(Sel[2]));
  // Probe on demultiplexer_6_out1
  // Probe on demultiplexer_7_out0
  Demultiplexer #(.enable("false")) demultiplexer_7 (
    .out0(demultiplexer_7_out0), .out1(demultiplexer_7_out1), .in(demultiplexer_3_out1), .sel(Sel[2]));
  // Probe on demultiplexer_7_out1

  // Notes on the sheet:
  //   DMux8Way
endmodule

module HalfAdder (
  input  a,
  input  b,
  output Sum,
  output Carry
);

  xor xor_1 (Sum, b, a);
  and and_1 (Carry, b, a);

  // Notes on the sheet:
  //   Half Adder
endmodule

module FullAdder (
  input  b,
  input  a,
  input  c,
  output Sum,
  output carry
);

  wire and_1_out, and_2_out, and_3_out, and_4_out, and_5_out, not_1_out, not_2_out, or_2_out, xor_1_out;

  xor xor_1 (xor_1_out, b, c);
  and and_1 (and_1_out, b, a);
  and and_2 (and_2_out, c, a);
  not not_1 (not_1_out, a);
  not not_2 (not_2_out, xor_1_out);
  and and_3 (and_3_out, c, b);
  and and_4 (and_4_out, xor_1_out, not_1_out);
  or or_1 (Sum, and_4_out, and_5_out);
  and and_5 (and_5_out, a, not_2_out);
  or or_2 (or_2_out, and_1_out, and_3_out);
  or or_3 (carry, or_2_out, and_2_out);

  // Notes on the sheet:
  //   Full Adder
endmodule

module Add16 (
  input  [15:0] a,
  input  [15:0] b,
  output [15:0] out
);

  wire fulladder_1_carry, fulladder_2_carry, fulladder_3_carry, fulladder_4_carry, fulladder_5_carry,
       fulladder_6_carry, fulladder_7_carry, fulladder_8_carry, fulladder_9_carry, fulladder_10_carry,
       fulladder_11_carry, fulladder_12_carry, fulladder_13_carry, fulladder_14_carry, fulladder_15_carry,
       halfadder_1_carry;

  HalfAdder halfadder_1 (.a(a[0]), .b(b[0]), .Sum(out[0]), .Carry(halfadder_1_carry));
  FullAdder fulladder_1 (.b(halfadder_1_carry), .a(a[1]), .c(a[2]), .Sum(out[1]), .carry(fulladder_1_carry));
  FullAdder fulladder_2 (.b(fulladder_1_carry), .a(a[2]), .c(a[3]), .Sum(out[2]), .carry(fulladder_2_carry));
  FullAdder fulladder_3 (.b(fulladder_2_carry), .a(a[3]), .c(a[4]), .Sum(out[3]), .carry(fulladder_3_carry));
  FullAdder fulladder_4 (.b(fulladder_3_carry), .a(a[4]), .c(b[4]), .Sum(out[4]), .carry(fulladder_4_carry));
  FullAdder fulladder_5 (.b(fulladder_4_carry), .a(a[5]), .c(a[6]), .Sum(out[5]), .carry(fulladder_5_carry));
  FullAdder fulladder_6 (.b(fulladder_5_carry), .a(a[6]), .c(b[6]), .Sum(out[6]), .carry(fulladder_6_carry));
  FullAdder fulladder_7 (.b(fulladder_6_carry), .a(a[7]), .c(a[8]), .Sum(out[7]), .carry(fulladder_7_carry));
  FullAdder fulladder_8 (.b(fulladder_7_carry), .a(a[8]), .c(a[9]), .Sum(out[8]), .carry(fulladder_8_carry));
  FullAdder fulladder_9 (.b(fulladder_8_carry), .a(a[9]), .c(a[10]), .Sum(out[9]), .carry(fulladder_9_carry));
  FullAdder fulladder_10 (.b(fulladder_9_carry), .a(a[10]), .c(a[11]), .Sum(out[10]), .carry(fulladder_10_carry));
  FullAdder fulladder_11 (.b(fulladder_10_carry), .a(a[11]), .c(a[12]), .Sum(out[11]), .carry(fulladder_11_carry));
  FullAdder fulladder_12 (.b(fulladder_11_carry), .a(a[12]), .c(a[13]), .Sum(out[12]), .carry(fulladder_12_carry));
  FullAdder fulladder_13 (.b(fulladder_12_carry), .a(a[13]), .c(a[14]), .Sum(out[13]), .carry(fulladder_13_carry));
  FullAdder fulladder_14 (.b(fulladder_13_carry), .a(a[14]), .c(a[15]), .Sum(out[14]), .carry(fulladder_14_carry));
  FullAdder fulladder_15 (.b(fulladder_14_carry), .a(a[15]), .c(b[15]), .Sum(out[15]), .carry(fulladder_15_carry));

  assign {b[14:7], b[5], b[3:1]} = {a[15:8], a[6], a[4:2]};

  // Notes on the sheet:
  //   Add16
  //   Overflow
endmodule

module Inc16 (
  input  [15:0] a,
  output [15:0] out
);

  wire fulladder_1_carry, fulladder_2_carry, fulladder_3_carry, fulladder_4_carry, fulladder_5_carry,
       fulladder_6_carry, fulladder_7_carry, fulladder_8_carry, fulladder_9_carry, fulladder_10_carry,
       fulladder_11_carry, fulladder_12_carry, fulladder_13_carry, fulladder_14_carry, fulladder_15_carry,
       halfadder_1_carry;

  HalfAdder halfadder_1 (.a(a[0]), .b(a[15]), .Sum(out[0]), .Carry(halfadder_1_carry));
  not not_1 (a[15], 1'b1);
  FullAdder fulladder_1 (.b(halfadder_1_carry), .a(a[1]), .c(a[15]), .Sum(out[1]), .carry(fulladder_1_carry));
  FullAdder fulladder_2 (.b(fulladder_1_carry), .a(a[15]), .c(a[15]), .Sum(out[2]), .carry(fulladder_2_carry));
  FullAdder fulladder_3 (.b(fulladder_2_carry), .a(a[15]), .c(a[15]), .Sum(out[3]), .carry(fulladder_3_carry));
  FullAdder fulladder_4 (.b(fulladder_3_carry), .a(a[15]), .c(a[15]), .Sum(out[4]), .carry(fulladder_4_carry));
  FullAdder fulladder_5 (.b(fulladder_4_carry), .a(a[5]), .c(a[15]), .Sum(out[5]), .carry(fulladder_5_carry));
  FullAdder fulladder_6 (.b(fulladder_5_carry), .a(a[15]), .c(a[15]), .Sum(out[6]), .carry(fulladder_6_carry));
  FullAdder fulladder_7 (.b(fulladder_6_carry), .a(a[7]), .c(a[15]), .Sum(out[7]), .carry(fulladder_7_carry));
  FullAdder fulladder_8 (.b(fulladder_7_carry), .a(a[15]), .c(a[15]), .Sum(out[8]), .carry(fulladder_8_carry));
  FullAdder fulladder_9 (.b(fulladder_8_carry), .a(a[15]), .c(a[15]), .Sum(out[9]), .carry(fulladder_9_carry));
  FullAdder fulladder_10 (.b(fulladder_9_carry), .a(a[15]), .c(a[15]), .Sum(out[10]), .carry(fulladder_10_carry));
  FullAdder fulladder_11 (.b(fulladder_10_carry), .a(a[15]), .c(a[15]), .Sum(out[11]), .carry(fulladder_11_carry));
  FullAdder fulladder_12 (.b(fulladder_11_carry), .a(a[15]), .c(a[15]), .Sum(out[12]), .carry(fulladder_12_carry));
  FullAdder fulladder_13 (.b(fulladder_12_carry), .a(a[15]), .c(a[15]), .Sum(out[13]), .carry(fulladder_13_carry));
  FullAdder fulladder_14 (.b(fulladder_13_carry), .a(a[15]), .c(a[15]), .Sum(out[14]), .carry(fulladder_14_carry));
  FullAdder fulladder_15 (.b(fulladder_14_carry), .a(a[15]), .c(a[15]), .Sum(out[15]), .carry(fulladder_15_carry));

  assign {a[14:8], a[6], a[4:2]} = {11{a[15]}};

  // Notes on the sheet:
  //   Inc16
endmodule

module ALU (
  input  [15:0] x,
  input  zx,
  input  nx,
  input  [15:0] y,
  input  no,
  input  zy,
  input  ny,
  input  f,
  output ng,
  output zr,
  output [15:0] out
);

  wire or8way_1_out, or8way_2_out, or_1_out;
  wire [15:0] adder_1_out, and_1_out, multiplexer_1_out, multiplexer_2_out, multiplexer_3_out,
       multiplexer_4_out, multiplexer_5_out, not_1_out, not_2_out, not_3_out;

  Multiplexer #(.width(16), .enable("false")) multiplexer_1 (
    .in0(x), .in1({16{1'b0}}), .out(multiplexer_1_out), .sel(zx));
  assign not_1_out = ~multiplexer_1_out;  // NOT_Gate not_1, 16 bits wide
  Multiplexer #(.width(16), .enable("false")) multiplexer_2 (
    .in0(y), .in1({16{1'b0}}), .out(multiplexer_2_out), .sel(zy));
  assign not_2_out = ~multiplexer_2_out;  // NOT_Gate not_2, 16 bits wide
  Multiplexer #(.width(16), .enable("false")) multiplexer_3 (
    .in0(multiplexer_1_out), .in1(not_1_out), .out(multiplexer_3_out), .sel(nx));
  Multiplexer #(.width(16), .enable("false")) multiplexer_4 (
    .in0(multiplexer_2_out), .in1(not_2_out), .out(multiplexer_4_out), .sel(ny));
  assign and_1_out = multiplexer_3_out & multiplexer_4_out;  // AND_Gate and_1, 16 bits wide
  Adder #(.width(16)) adder_1 (.a(multiplexer_3_out), .b(multiplexer_4_out), .out(adder_1_out));  // open: cin, cout
  Multiplexer #(.width(16), .enable("false")) multiplexer_5 (
    .in0(and_1_out), .in1(adder_1_out), .out(multiplexer_5_out), .sel(f));
  assign not_3_out = ~multiplexer_5_out;  // NOT_Gate not_3, 16 bits wide
  Multiplexer #(.width(16), .enable("false")) multiplexer_6 (
    .in0(multiplexer_5_out), .in1(not_3_out), .out({ng, out[14:0]}), .sel(no));
  Or8Way or8way_1 (.in_1(out[7:0]), .Out(or8way_1_out));
  or or_1 (or_1_out, or8way_1_out, or8way_2_out);
  Or8Way or8way_2 (.in_1({ng, out[14:8]}), .Out(or8way_2_out));
  not not_4 (zr, or_1_out);

  assign out[15] = ng;

  // Notes on the sheet:
  //   Zero
  //   ALU
  //   Negate
  //   Add/And
  //   Negate
  //   Is negative?
  //   Is zero?
endmodule

module Bit (
  input  in,
  input  load,
  output out
);

  wire clock_1_out, multiplexer_1_out;

  Clock clock_1 (.out(clock_1_out));
  Multiplexer #(.enable("false")) multiplexer_1 (.in0(in), .in1(out), .out(multiplexer_1_out), .sel(load));
  D_Flip_Flop d_ff_1 (.clk(clock_1_out), .D(multiplexer_1_out), .Q(out));  // open: Qn, preset, en, reset

  // Notes on the sheet:
  //   BIT
endmodule

module Register (
  input  load,
  input  [15:0] in,
  output [15:0] out
);

  Bit bit_1 (.in(in[0]), .load(load), .out(out[0]));
  Bit bit_2 (.in(in[1]), .load(load), .out(out[1]));
  Bit bit_3 (.in(in[2]), .load(load), .out(out[2]));
  Bit bit_4 (.in(in[3]), .load(load), .out(out[3]));
  Bit bit_5 (.in(in[4]), .load(load), .out(out[4]));
  Bit bit_6 (.in(in[5]), .load(load), .out(out[5]));
  Bit bit_7 (.in(in[6]), .load(load), .out(out[6]));
  Bit bit_8 (.in(in[7]), .load(load), .out(out[7]));
  Bit bit_9 (.in(in[8]), .load(load), .out(out[8]));
  Bit bit_10 (.in(in[9]), .load(load), .out(out[9]));
  Bit bit_11 (.in(in[10]), .load(load), .out(out[10]));
  Bit bit_12 (.in(in[11]), .load(load), .out(out[11]));
  Bit bit_13 (.in(in[12]), .load(load), .out(out[12]));
  Bit bit_14 (.in(in[13]), .load(load), .out(out[13]));
  Bit bit_15 (.in(in[14]), .load(load), .out(out[14]));
  Bit bit_16 (.in(in[15]), .load(load), .out(out[15]));

  // Notes on the sheet:
  //   REGISTER
  //   BIT
endmodule

module Ram8 (
  input  Load,
  input  [2:0] Address,
  input  [15:0] In,
  output [15:0] Out
);

  wire [15:0] demultiplexer_1_out0, demultiplexer_1_out1, demultiplexer_1_out2, demultiplexer_1_out3,
       demultiplexer_1_out4, demultiplexer_1_out5, demultiplexer_1_out6, demultiplexer_1_out7,
       register_1_out, register_2_out, register_3_out, register_4_out, register_5_out, register_6_out,
       register_7_out, register_8_out;

  Demultiplexer #(.select(3), .width(16), .enable("false")) demultiplexer_1 (
    .out0(demultiplexer_1_out0), .out1(demultiplexer_1_out1), .out2(demultiplexer_1_out2),
    .out3(demultiplexer_1_out3), .out4(demultiplexer_1_out4), .out5(demultiplexer_1_out5),
    .out6(demultiplexer_1_out6), .out7(demultiplexer_1_out7), .in(In), .sel(Address));
  Register register_1 (.load(Load), .in(demultiplexer_1_out0), .out(register_1_out));
  Register register_2 (.load(Load), .in(demultiplexer_1_out1), .out(register_2_out));
  Register register_3 (.load(Load), .in(demultiplexer_1_out2), .out(register_3_out));
  Register register_4 (.load(Load), .in(demultiplexer_1_out3), .out(register_4_out));
  Register register_5 (.load(Load), .in(demultiplexer_1_out4), .out(register_5_out));
  Register register_6 (.load(Load), .in(demultiplexer_1_out5), .out(register_6_out));
  Register register_7 (.load(Load), .in(demultiplexer_1_out6), .out(register_7_out));
  Register register_8 (.load(Load), .in(demultiplexer_1_out7), .out(register_8_out));
  Multiplexer #(.select(3), .width(16), .enable("false")) multiplexer_1 (
    .in0(register_1_out), .in1(register_2_out), .in2(register_3_out), .in3(register_4_out),
    .in4(register_5_out), .in5(register_6_out), .in6(register_7_out), .in7(register_8_out), .out(Out),
    .sel(Address));

  // Notes on the sheet:
  //   RAM8
endmodule

module Ram64 (
  input  Load,
  input  [5:0] Address,
  input  [15:0] In,
  output [15:0] Out
);

  wire clock_1_out;
  wire [15:0] demultiplexer_1_out0, demultiplexer_1_out1, demultiplexer_1_out2, demultiplexer_1_out3,
       demultiplexer_1_out4, demultiplexer_1_out5, demultiplexer_1_out6, demultiplexer_1_out7, ram_1_data,
       ram_2_data, ram_3_data, ram_4_data, ram_5_data, ram_6_data, ram_7_data, ram_8_data;

  Demultiplexer #(.select(3), .width(16), .enable("false")) demultiplexer_1 (
    .out0(demultiplexer_1_out0), .out1(demultiplexer_1_out1), .out2(demultiplexer_1_out2),
    .out3(demultiplexer_1_out3), .out4(demultiplexer_1_out4), .out5(demultiplexer_1_out5),
    .out6(demultiplexer_1_out6), .out7(demultiplexer_1_out7), .in(In), .sel(Address[5:3]));
  RAM #(.addrWidth(3), .dataWidth(16), .bus("separate")) ram_1 (
    .addr(Address[2:0]), .din(demultiplexer_1_out0), .data(ram_1_data), .str(Load), .clk(clock_1_out));  // open: sel, ld, clr
  RAM #(.addrWidth(3), .dataWidth(16), .bus("separate")) ram_2 (
    .addr(Address[2:0]), .din(demultiplexer_1_out1), .data(ram_2_data), .str(Load), .clk(clock_1_out));  // open: sel, ld, clr
  RAM #(.addrWidth(3), .dataWidth(16), .bus("separate")) ram_3 (
    .addr(Address[2:0]), .din(demultiplexer_1_out2), .data(ram_3_data), .str(Load), .clk(clock_1_out));  // open: sel, ld, clr
  RAM #(.addrWidth(3), .dataWidth(16), .bus("separate")) ram_4 (
    .addr(Address[2:0]), .din(demultiplexer_1_out3), .data(ram_4_data), .str(Load), .clk(clock_1_out));  // open: sel, ld, clr
  RAM #(.addrWidth(3), .dataWidth(16), .bus("separate")) ram_5 (
    .addr(Address[2:0]), .din(demultiplexer_1_out4), .data(ram_5_data), .str(Load), .clk(clock_1_out));  // open: sel, ld, clr
  RAM #(.addrWidth(3), .dataWidth(16), .bus("separate")) ram_6 (
    .addr(Address[2:0]), .din(demultiplexer_1_out5), .data(ram_6_data), .str(Load), .clk(clock_1_out));  // open: sel, ld, clr
  RAM #(.addrWidth(3), .dataWidth(16), .bus("separate")) ram_7 (
    .addr(Address[2:0]), .din(demultiplexer_1_out6), .data(ram_7_data), .str(Load), .clk(clock_1_out));  // open: sel, ld, clr
  RAM #(.addrWidth(3), .dataWidth(16), .bus("separate")) ram_8 (
    .addr(Address[2:0]), .din(demultiplexer_1_out7), .data(ram_8_data), .str(Load), .clk(clock_1_out));  // open: sel, ld, clr
  Clock clock_1 (.out(clock_1_out));
  Multiplexer #(.select(3), .width(16), .enable("false")) multiplexer_1 (
    .in0(ram_1_data), .in1(ram_2_data), .in2(ram_3_data), .in3(ram_4_data), .in4(ram_5_data),
    .in5(ram_6_data), .in6(ram_7_data), .in7(ram_8_data), .out(Out), .sel(Address[5:3]));

  // Notes on the sheet:
  //   RAM64
endmodule

module RAM512 (
  input  Load,
  input  [8:0] Address,
  input  [15:0] In,
  output [15:0] Out
);

  wire clock_1_out;
  wire [15:0] demultiplexer_1_out0, demultiplexer_1_out1, demultiplexer_1_out2, demultiplexer_1_out3,
       demultiplexer_1_out4, demultiplexer_1_out5, demultiplexer_1_out6, demultiplexer_1_out7, ram_1_data,
       ram_2_data, ram_3_data, ram_4_data, ram_5_data, ram_6_data, ram_7_data, ram_8_data;

  Demultiplexer #(.select(3), .width(16), .enable("false")) demultiplexer_1 (
    .out0(demultiplexer_1_out0), .out1(demultiplexer_1_out1), .out2(demultiplexer_1_out2),
    .out3(demultiplexer_1_out3), .out4(demultiplexer_1_out4), .out5(demultiplexer_1_out5),
    .out6(demultiplexer_1_out6), .out7(demultiplexer_1_out7), .in(In), .sel(Address[8:6]));
  RAM #(.addrWidth(6), .dataWidth(16), .bus("separate")) ram_1 (
    .addr(Address[5:0]), .din(demultiplexer_1_out0), .data(ram_1_data), .str(Load), .clk(clock_1_out));  // open: sel, ld, clr
  RAM #(.addrWidth(6), .dataWidth(16), .bus("separate")) ram_2 (
    .addr(Address[5:0]), .din(demultiplexer_1_out1), .data(ram_2_data), .str(Load), .clk(clock_1_out));  // open: sel, ld, clr
  RAM #(.addrWidth(6), .dataWidth(16), .bus("separate")) ram_3 (
    .addr(Address[5:0]), .din(demultiplexer_1_out2), .data(ram_3_data), .str(Load), .clk(clock_1_out));  // open: sel, ld, clr
  RAM #(.addrWidth(6), .dataWidth(16), .bus("separate")) ram_4 (
    .addr(Address[5:0]), .din(demultiplexer_1_out3), .data(ram_4_data), .str(Load), .clk(clock_1_out));  // open: sel, ld, clr
  RAM #(.addrWidth(6), .dataWidth(16), .bus("separate")) ram_5 (
    .addr(Address[5:0]), .din(demultiplexer_1_out4), .data(ram_5_data), .str(Load), .clk(clock_1_out));  // open: sel, ld, clr
  RAM #(.addrWidth(6), .dataWidth(16), .bus("separate")) ram_6 (
    .addr(Address[5:0]), .din(demultiplexer_1_out5), .data(ram_6_data), .str(Load), .clk(clock_1_out));  // open: sel, ld, clr
  RAM #(.addrWidth(6), .dataWidth(16), .bus("separate")) ram_7 (
    .addr(Address[5:0]), .din(demultiplexer_1_out6), .data(ram_7_data), .str(Load), .clk(clock_1_out));  // open: sel, ld, clr
  RAM #(.addrWidth(6), .dataWidth(16), .bus("separate")) ram_8 (
    .addr(Address[5:0]), .din(demultiplexer_1_out7), .data(ram_8_data), .str(Load), .clk(clock_1_out));  // open: sel, ld, clr
  Clock clock_1 (.out(clock_1_out));
  Multiplexer #(.select(3), .width(16), .enable("false")) multiplexer_1 (
    .in0(ram_1_data), .in1(ram_2_data), .in2(ram_3_data), .in3(ram_4_data), .in4(ram_5_data),
    .in5(ram_6_data), .in6(ram_7_data), .in7(ram_8_data), .out(Out), .sel(Address[8:6]));

  // Notes on the sheet:
  //   RAM512
endmodule

module RAM4k (
  input  Load,
  input  [11:0] Address,
  input  [15:0] In,
  output [15:0] Out
);

  wire clock_1_out;
  wire [15:0] demultiplexer_1_out0, demultiplexer_1_out1, demultiplexer_1_out2, demultiplexer_1_out3,
       demultiplexer_1_out4, demultiplexer_1_out5, demultiplexer_1_out6, demultiplexer_1_out7, ram_1_data,
       ram_2_data, ram_3_data, ram_4_data, ram_5_data, ram_6_data, ram_7_data, ram_8_data;

  Demultiplexer #(.select(3), .width(16), .enable("false")) demultiplexer_1 (
    .out0(demultiplexer_1_out0), .out1(demultiplexer_1_out1), .out2(demultiplexer_1_out2),
    .out3(demultiplexer_1_out3), .out4(demultiplexer_1_out4), .out5(demultiplexer_1_out5),
    .out6(demultiplexer_1_out6), .out7(demultiplexer_1_out7), .in(In), .sel(Address[11:9]));
  RAM #(.addrWidth(9), .dataWidth(16), .bus("separate")) ram_1 (
    .addr(Address[8:0]), .din(demultiplexer_1_out0), .data(ram_1_data), .str(Load), .clk(clock_1_out));  // open: sel, ld, clr
  RAM #(.addrWidth(9), .dataWidth(16), .bus("separate")) ram_2 (
    .addr(Address[8:0]), .din(demultiplexer_1_out1), .data(ram_2_data), .str(Load), .clk(clock_1_out));  // open: sel, ld, clr
  RAM #(.addrWidth(9), .dataWidth(16), .bus("separate")) ram_3 (
    .addr(Address[8:0]), .din(demultiplexer_1_out2), .data(ram_3_data), .str(Load), .clk(clock_1_out));  // open: sel, ld, clr
  RAM #(.addrWidth(9), .dataWidth(16), .bus("separate")) ram_4 (
    .addr(Address[8:0]), .din(demultiplexer_1_out3), .data(ram_4_data), .str(Load), .clk(clock_1_out));  // open: sel, ld, clr
  RAM #(.addrWidth(9), .dataWidth(16), .bus("separate")) ram_5 (
    .addr(Address[8:0]), .din(demultiplexer_1_out4), .data(ram_5_data), .str(Load), .clk(clock_1_out));  // open: sel, ld, clr
  RAM #(.addrWidth(9), .dataWidth(16), .bus("separate")) ram_6 (
    .addr(Address[8:0]), .din(demultiplexer_1_out5), .data(ram_6_data), .str(Load), .clk(clock_1_out));  // open: sel, ld, clr
  RAM #(.addrWidth(9), .dataWidth(16), .bus("separate")) ram_7 (
    .addr(Address[8:0]), .din(demultiplexer_1_out6), .data(ram_7_data), .str(Load), .clk(clock_1_out));  // open: sel, ld, clr
  RAM #(.addrWidth(9), .dataWidth(16), .bus("separate")) ram_8 (
    .addr(Address[8:0]), .din(demultiplexer_1_out7), .data(ram_8_data), .str(Load), .clk(clock_1_out));  // open: sel, ld, clr
  Clock clock_1 (.out(clock_1_out));
  Multiplexer #(.select(3), .width(16), .enable("false")) multiplexer_1 (
    .in0(ram_1_data), .in1(ram_2_data), .in2(ram_3_data), .in3(ram_4_data), .in4(ram_5_data),
    .in5(ram_6_data), .in6(ram_7_data), .in7(ram_8_data), .out(Out), .sel(Address[11:9]));

  // Notes on the sheet:
  //   RAM4k
endmodule

module RAM16k (
  input  Load,
  input  [14:0] Address,
  input  [15:0] In,
  output [15:0] Out
);

  wire clock_1_out;
  wire [15:0] demultiplexer_1_out0, demultiplexer_1_out1, demultiplexer_1_out2, demultiplexer_1_out3,
       demultiplexer_1_out4, demultiplexer_1_out5, demultiplexer_1_out6, demultiplexer_1_out7, ram_1_data,
       ram_2_data, ram_3_data, ram_4_data, ram_5_data, ram_6_data, ram_7_data, ram_8_data;

  Demultiplexer #(.select(3), .width(16), .enable("false")) demultiplexer_1 (
    .out0(demultiplexer_1_out0), .out1(demultiplexer_1_out1), .out2(demultiplexer_1_out2),
    .out3(demultiplexer_1_out3), .out4(demultiplexer_1_out4), .out5(demultiplexer_1_out5),
    .out6(demultiplexer_1_out6), .out7(demultiplexer_1_out7), .in(In), .sel(Address[14:12]));
  RAM #(.addrWidth(12), .dataWidth(16), .bus("separate")) ram_1 (
    .addr(Address[11:0]), .din(demultiplexer_1_out0), .data(ram_1_data), .str(Load), .clk(clock_1_out));  // open: sel, ld, clr
  RAM #(.addrWidth(12), .dataWidth(16), .bus("separate")) ram_2 (
    .addr(Address[11:0]), .din(demultiplexer_1_out1), .data(ram_2_data), .str(Load), .clk(clock_1_out));  // open: sel, ld, clr
  RAM #(.addrWidth(12), .dataWidth(16), .bus("separate")) ram_3 (
    .addr(Address[11:0]), .din(demultiplexer_1_out2), .data(ram_3_data), .str(Load), .clk(clock_1_out));  // open: sel, ld, clr
  RAM #(.addrWidth(12), .dataWidth(16), .bus("separate")) ram_4 (
    .addr(Address[11:0]), .din(demultiplexer_1_out3), .data(ram_4_data), .str(Load), .clk(clock_1_out));  // open: sel, ld, clr
  RAM #(.addrWidth(12), .dataWidth(16), .bus("separate")) ram_5 (
    .addr(Address[11:0]), .din(demultiplexer_1_out4), .data(ram_5_data), .str(Load), .clk(clock_1_out));  // open: sel, ld, clr
  RAM #(.addrWidth(12), .dataWidth(16), .bus("separate")) ram_6 (
    .addr(Address[11:0]), .din(demultiplexer_1_out5), .data(ram_6_data), .str(Load), .clk(clock_1_out));  // open: sel, ld, clr
  RAM #(.addrWidth(12), .dataWidth(16), .bus("separate")) ram_7 (
    .addr(Address[11:0]), .din(demultiplexer_1_out6), .data(ram_7_data), .str(Load), .clk(clock_1_out));  // open: sel, ld, clr
  RAM #(.addrWidth(12), .dataWidth(16), .bus("separate")) ram_8 (
    .addr(Address[11:0]), .din(demultiplexer_1_out7), .data(ram_8_data), .str(Load), .clk(clock_1_out));  // open: sel, ld, clr
  Clock clock_1 (.out(clock_1_out));
  Multiplexer #(.select(3), .width(16), .enable("false")) multiplexer_1 (
    .in0(ram_1_data), .in1(ram_2_data), .in2(ram_3_data), .in3(ram_4_data), .in4(ram_5_data),
    .in5(ram_6_data), .in6(ram_7_data), .in7(ram_8_data), .out(Out), .sel(Address[14:12]));

  // Notes on the sheet:
  //   RAM16k
endmodule

module PC (
  input  [15:0] IN,
  input  Inc,
  input  Load,
  input  Reset,
  output [15:0] out_5
);

  wire clock_1_out;
  wire [15:0] adder_1_out, multiplexer_1_out, multiplexer_2_out, multiplexer_3_out;

  Multiplexer #(.width(16), .enable("false")) multiplexer_1 (
    .in0(out_5), .in1(adder_1_out), .out(multiplexer_1_out), .sel(Inc));
  Adder #(.width(16)) adder_1 (.a(out_5), .b(16'h1), .out(adder_1_out));  // open: cin, cout
  Multiplexer #(.width(16), .enable("false")) multiplexer_2 (
    .in0(multiplexer_1_out), .in1(IN), .out(multiplexer_2_out), .sel(Load));
  Multiplexer #(.width(16), .enable("false")) multiplexer_3 (
    .in0(multiplexer_2_out), .in1({16{1'b0}}), .out(multiplexer_3_out), .sel(Reset));
  Clock clock_1 (.out(clock_1_out));
  Register_part #(.width(16)) register_1 (.D(multiplexer_3_out), .en(1'b1), .Q(out_5), .clk(clock_1_out));  // open: clr

  // Notes on the sheet:
  //   PC
endmodule

module Memory (
  input  Load,
  input  [15:0] In,
  input  [14:0] Address,
  output [15:0] Out
);

  wire clock_1_out, demultiplexer_1_out0, demultiplexer_1_out1, demultiplexer_1_out2, demultiplexer_1_out3,
       or_1_out;
  wire [15:0] ram_1_data, ram_2_data, register_1_q;

  Clock clock_1 (.out(clock_1_out));
  Demultiplexer #(.select(2), .enable("false")) demultiplexer_1 (
    .out0(demultiplexer_1_out0), .out1(demultiplexer_1_out1), .out2(demultiplexer_1_out2),
    .out3(demultiplexer_1_out3), .in(Load), .sel(Address[14:13]));
  or or_1 (or_1_out, demultiplexer_1_out0, demultiplexer_1_out1);
  Register_part #(.width(16)) register_1 (
    .D(In), .en(demultiplexer_1_out3), .Q(register_1_q), .clk(clock_1_out));  // open: clr
  RAM #(.addrWidth(13), .dataWidth(16), .bus("separate")) ram_1 (
    .addr(Address[12:0]), .din(In), .data(ram_1_data), .clk(clock_1_out), .ld(or_1_out));  // open: str, sel, clr
  RAM #(.addrWidth(12), .dataWidth(16), .bus("separate")) ram_2 (
    .addr(Address[11:0]), .din(In), .data(ram_2_data), .clk(clock_1_out), .ld(demultiplexer_1_out2));  // open: str, sel, clr
  Multiplexer #(.select(2), .width(16), .enable("false")) multiplexer_1 (
    .in0(ram_1_data), .in1(ram_1_data), .in2(ram_2_data), .in3(register_1_q), .out(Out), .sel(Address[14:13]));
endmodule

module CPU (
  input  [15:0] imstructiom,
  input  [15:0] inM,
  input  Load,
  output [14:0] out_4,
  output [15:0] outM,
  output [14:0] pc,
  output WriteM
);

  wire alu_1_ng, alu_1_zr, and_1_out, and_3_out, and_4_out, and_5_out, and_6_out, not_2_out, not_3_out,
       not_4_out, or_1_out, or_2_out, or_3_out;
  wire [15:0] multiplexer_1_out, multiplexer_2_out, register_2_q;
  wire [15:15] not_1_out, pc_1_out_5, register_1_q;

  not not_1 (not_1_out[15], 1'b1);
  Multiplexer #(.width(16), .enable("false")) multiplexer_1 (
    .in0({not_1_out[15], imstructiom[14:0]}), .in1(outM), .out(multiplexer_1_out), .sel(imstructiom[15]));
  not not_2 (not_2_out, imstructiom[15]);
  Register_part #(.width(16)) register_1 (
    .D(multiplexer_1_out), .en(or_1_out), .Q({register_1_q[15], out_4}));  // open: clk, clr
  or or_1 (or_1_out, not_2_out, imstructiom[5]);
  and and_1 (and_1_out, imstructiom[15], imstructiom[4]);
  and and_2 (WriteM, imstructiom[15], imstructiom[3]);
  Multiplexer #(.width(16), .enable("false")) multiplexer_2 (
    .in0({register_1_q[15], out_4}), .in1(inM), .out(multiplexer_2_out), .sel(imstructiom[12]));
  Register_part #(.width(16)) register_2 (.D(outM), .en(and_1_out), .Q(register_2_q));  // open: clk, clr
  or or_2 (or_2_out, alu_1_zr, alu_1_ng);
  not not_3 (not_3_out, or_2_out);
  not not_4 (not_4_out, and_6_out);
  and and_3 (and_3_out, imstructiom[1], alu_1_zr);
  and and_4 (and_4_out, imstructiom[0], alu_1_ng);
  and and_5 (and_5_out, imstructiom[2], not_3_out);
  PC pc_1 (.IN(register_2_q), .Inc(and_6_out), .Load(not_4_out), .Reset(Load), .out_5({pc_1_out_5[15], pc}));
  and and_6 (and_6_out, imstructiom[15], or_3_out);
  or or_3 (or_3_out, and_3_out, and_4_out, and_5_out);
  ALU alu_1 (
    .x(register_2_q), .zx(imstructiom[11]), .nx(imstructiom[10]), .y(multiplexer_2_out), .no(imstructiom[6]),
    .zy(imstructiom[9]), .ny(imstructiom[8]), .f(imstructiom[7]), .ng(alu_1_ng), .zr(alu_1_zr), .out(outM));
endmodule

module Computer (
  input  Reset
);

  wire CPU_writem;
  wire [14:0] CPU_out_4, CPU_pc;
  wire [15:0] CPU_outm, Memory_out, rom_1_data;

  Memory Memory (.Load(CPU_writem), .In(CPU_outm), .Address(CPU_out_4), .Out(Memory_out));
  CPU CPU (
    .imstructiom(rom_1_data), .inM(Memory_out), .Load(Reset), .out_4(CPU_out_4), .outM(CPU_outm),
    .pc(CPU_pc), .WriteM(CPU_writem));
  ROM #(.addrWidth(15), .dataWidth(16)) rom_1 (.addr(CPU_pc), .data(rom_1_data));  // open: sel
endmodule
